// Logisim project ex2.circ as structural Verilog: 1 circuit, main circuit AddMachine
module AddMachine (
  output [7:0] ADD_OUT,
  output [7:0] REG_OUT
);

  wire clock_1_out, undriven;

  Adder adder_1 (.a(REG_OUT), .b(8'h11), .out(ADD_OUT));  // open: cin, cout
  Clock clock_1 (.out(clock_1_out));
  Register register_1 (.D(ADD_OUT), .clk(clock_1_out), .Q(REG_OUT), .clr(undriven));  // open: en

  // Notes on the sheet:
  //   PUT CIRCUITRY HERE
endmodule
